# Fritzing sketch Genius-Arduino (saved by Fritzing 0.9.2b)
circuit board: 8.46667cm x 5.64444cm
breadboards: 1

parts:
  Componente1 = Arduino Uno (Rev3)
  LED1 = smd LED [color="Red (633nm)" package="1206 [SMD]"]
  R1 = Resistor [tolerance=±5% resistance=330 package=THT]
  S1 = Pushbutton [package="[THT]"]

nets (from the breadboard view):
  N1: Componente1.D10_PWM/SS, S1.Pin_3, S1.Pin_4
  N2: Componente1.D5_PWM, LED1.anode
  N3: Componente1.GND, R1.Pin_0, S1.Pin_1, S1.Pin_2
  N4: LED1.cathode, R1.Pin_1
